// Logisim project compuertaXNOR.circ as structural Verilog: 1 circuit, main circuit main
module main (
  input  in_1,
  input  B,
  output out_3
);

  wire transistor_1_out, transistor_2_out;

  Transistor transistor_1 (.in(1'b1), .out(transistor_1_out), .gate(in_1));
  Transistor #(.\type ("n"), .gate("br")) transistor_2 (.in(1'b1), .out(transistor_2_out), .gate(in_1));
  Transistor transistor_3 (.in(transistor_1_out), .out(out_3), .gate(B));
  Transistor #(.\type ("n"), .gate("br")) transistor_4 (.in(transistor_2_out), .out(out_3), .gate(B));
  Pull_Resistor pull_resistor_1 (.node(out_3));

  // Notes on the sheet:
  //   NEG B
  //   A
  //   NEG A
endmodule
