// Logisim project ejercicio1.circ as structural Verilog: 1 circuit, main circuit main
module main (
  input  in_1,
  input  P,
  input  Q,
  input  in_4,
  input  P_2,
  input  in_6,
  input  Q_2,
  output out_8,
  output out_9,
  output out_10,
  output out_11
);

  wire not_1_out, transistor_1_out;

  not not_1 (not_1_out, P);
  Transistor transistor_1 (.in(1'b1), .out(transistor_1_out), .gate(P_2));
  Pull_Resistor pull_resistor_1 (.node(transistor_1_out));
  or or_1 (out_8, not_1_out, Q);
  Transistor #(.\type ("n")) transistor_2 (.in(1'b1), .out(out_10), .gate(transistor_1_out));
  Transistor #(.\type ("n"), .gate("br")) transistor_3 (.in(1'b1), .out(out_10), .gate(Q_2));
  Pull_Resistor pull_resistor_2 (.node(out_10));
  Transistor #(.\type ("n")) transistor_4 (.in(1'b1), .out(out_9), .gate(in_1));
  Transistor #(.\type ("n"), .gate("br")) transistor_5 (.in(1'b1), .out(out_9), .gate(in_4));
  Transistor transistor_6 (.in(1'b1), .out(out_11), .gate(in_6));
  Pull_Resistor pull_resistor_3 (.node(out_11));
  Pull_Resistor pull_resistor_4 (.node(out_9));

  // Notes on the sheet:
  //   ARRIETA MANCERA LUIS SEBASTIAN 318174116
  //   P -> Q  = NEG P v Q
  //   P -> Q con compuerta OR y NOT implementada
  //   Compuerta OR implementada
  //   Compuerta NOT Implementada
endmodule
