// Logisim project negacionNOT.circ as structural Verilog: 1 circuit, main circuit main
module main (
  input  in_1,
  output out_2
);

  Transistor transistor_1 (.in(1'b1), .out(out_2), .gate(in_1));
  Pull_Resistor pull_resistor_1 (.node(out_2));
endmodule
