// Logisim project practica03.circ as structural Verilog: 1 circuit, main circuit main
module main (
  input  in_1,
  input  P,
  input  in_3,
  input  in_4,
  input  Q,
  input  in_6,
  input  B,
  input  A0,
  input  A1,
  input  B0,
  input  B1,
  output out_12,
  output out_13,
  output out_14,
  output out_15,
  output A___B,
  output A___B_2,
  output A___B_3
);

  wire and_2_out, and_3_out, and_4_out, and_5_out, and_6_out, and_7_out, not_1_out, not_2_out, not_3_out,
       not_4_out, not_5_out, not_6_out, transistor_1_out, transistor_2_out, transistor_3_out, xnor_1_out,
       xnor_2_out;

  Transistor transistor_1 (.in(1'b1), .out(transistor_1_out), .gate(P));
  Transistor transistor_2 (.in(1'b1), .out(transistor_2_out), .gate(in_6));
  Transistor #(.\type ("n"), .gate("br")) transistor_3 (.in(1'b1), .out(transistor_3_out), .gate(in_6));
  Pull_Resistor pull_resistor_1 (.node(transistor_1_out));
  Transistor transistor_4 (.in(transistor_2_out), .out(out_15), .gate(B));
  Transistor #(.\type ("n"), .gate("br")) transistor_5 (.in(transistor_3_out), .out(out_15), .gate(B));
  Pull_Resistor pull_resistor_2 (.node(out_15));
  not not_1 (not_1_out, B0);
  not not_2 (not_2_out, B1);
  not not_3 (not_3_out, B0);
  not not_4 (not_4_out, B1);
  xnor xnor_1 (xnor_1_out, A0, B0);
  xnor xnor_2 (xnor_2_out, A1, B1);
  not not_5 (not_5_out, A0);
  not not_6 (not_6_out, A1);
  Transistor #(.\type ("n")) transistor_6 (.in(1'b1), .out(out_13), .gate(transistor_1_out));
  Transistor #(.\type ("n"), .gate("br")) transistor_7 (.in(1'b1), .out(out_13), .gate(Q));
  and and_1 (A___B_2, xnor_1_out, xnor_2_out);
  Pull_Resistor pull_resistor_3 (.node(out_13));
  and and_2 (and_2_out, A0, not_1_out);
  and and_3 (and_3_out, A0, A1, not_2_out);
  and and_4 (and_4_out, A1, not_3_out, not_4_out);
  and and_5 (and_5_out, not_5_out, not_6_out, B1);
  and and_6 (and_6_out, not_5_out, B0);
  and and_7 (and_7_out, not_6_out, B0, B1);
  Transistor transistor_8 (.in(1'b1), .out(out_14), .gate(in_4));
  Transistor #(.\type ("n")) transistor_9 (.in(1'b1), .out(out_12), .gate(in_1));
  Transistor #(.\type ("n"), .gate("br")) transistor_10 (.in(1'b1), .out(out_12), .gate(in_3));
  Pull_Resistor pull_resistor_4 (.node(out_14));
  or or_1 (A___B_3, and_5_out, and_6_out, and_7_out);
  Pull_Resistor pull_resistor_5 (.node(out_12));
  or or_2 (A___B, and_2_out, and_3_out, and_4_out);

  // Notes on the sheet:
  //   ACTIVIDAD 9.1
  //   ACTIVIDAD 9.2
  //   Numero A
  //   Numero B
  //   COMPUERTA XNOR CON TRANSISTORES
  //   p-type
  //   ARRIETA MANCERA LUIS SEBASTIAN 318174116
  //   P -> Q con compuerta OR y NOT implementada
  //   n-type
  //   A
  //   COMPARADOR BIRNARIO A > B   A = B   A < B
  //   p-type
  //   n-type
  //   B0
  //   B1
  //   A0
  //   B0
  //   A1
  //   B1
  //   A0
  //   A1
  //   NEG P
  //   COMPUERTA OR
  //   B0
  //   B1
  //   A0
  //   NEG B0
  //   A0
  //   A1
  //   NEG B1
  //   A1
  //   NEG B0
  //   NEG B1
  //   NEG A0
  //   NEG A1
  //   B1
  //   NEG A0
  //   NEG A1
  //   B0
  //   B0
  //   B1
  //   Compuerta OR implementada
  //   Compuerta NOT Implementada
endmodule
